# Fritzing sketch IRemettitore (saved by Fritzing 0.9.3b)
breadboards: 1

parts:
  Componente1 = Arduino Uno (Rev3)
  LED1 = LEDs [package=led10mm]
  LED2 = smd LED [color="Red (633nm)" package="0603 [SMD]"]
  R1 = Resistor [tolerance=±5% resistance=10k package="2512 [SMD]"]
  R2 = Resistor [tolerance=±5% resistance=100 package=THT]

nets:
  N1: Componente1.A0, LED1.C, R1.Pin_0
  N2: Componente1.D9_PWM, R2.Pin_1
  N3: Componente1.5V, R1.Pin_1
  N4: Componente1.GND, LED1.A, LED2.cathode
  N5: LED2.anode, R2.Pin_0
